# Fritzing sketch circuit-social-thermometer (saved by Fritzing 0.9.4)
breadboards: 1

parts:
  Part1 = Arduino Nano (Rev3.0)
  LED1 = LED - 5mm [color="White (8000K)" package="5 mm [THT]"]
  LED2 = LED - 5mm [color="White (8000K)" package="5 mm [THT]"]
  LED3 = LED - 5mm [color="White (8000K)" package="5 mm [THT]"]
  BAT1 = Battery Holders [package=battery-aa-kit]
  BAT2 = Battery Holders [package=battery-aa-kit]
  BAT3 = Battery Holders [package=battery-aa-kit]

nets:
  N1: Part1.GND, LED1.cathode, LED2.cathode, LED3.cathode, BAT3.-
  N2: Part1.D3, LED1.anode
  N3: Part1.D4, LED2.anode
  N4: Part1.D5, LED3.anode
  N5: Part1.5V, BAT1.+
  N6: BAT1.-, BAT2.+
  N7: BAT2.-, BAT3.+
